# Fritzing sketch Breadboard Setup v2 (saved by Fritzing 0.9.0b)
breadboards: 1

parts:
  R1 = Resistor [tolerance=±5% resistance=220 package=THT]
  Q1 = MOSFET-NCHANNEL [package=to-92]
  Q2 = MOSFET-NCHANNEL [package=to-92]
  Q3 = MOSFET-NCHANNEL [package=to-92]
  Q4 = MOSFET-NCHANNEL [package=to-92]
  Q5 = MOSFET-NCHANNEL [package=to-92]
  Q6 = MOSFET-NCHANNEL [package=to-92]
  R2 = Resistor [tolerance=±5% resistance=220 package=THT]
  R3 = Resistor [tolerance=±5% resistance=220 package=THT]
  R4 = Resistor [tolerance=±5% resistance=220 package=THT]
  R5 = Resistor [tolerance=±5% resistance=220 package=THT]
  R6 = Resistor [tolerance=±5% resistance=220 package=THT]
  R7 = Resistor [tolerance=±5% resistance=1M package=THT]
  R8 = Resistor [tolerance=±5% resistance=1M package=THT]
  R9 = Resistor [tolerance=±5% resistance=1M package=THT]
  R10 = Resistor [tolerance=±5% resistance=1M package=THT]
  R11 = Resistor [tolerance=±5% resistance=1M package=THT]
  R12 = Resistor [tolerance=±5% resistance=1M package=THT]
  P1 = S1133 Si Photodiode [package="8mm Ceramic [THT]"]
  P2 = S1133 Si Photodiode [package="8mm Ceramic [THT]"]
  P3 = S1133 Si Photodiode [package="8mm Ceramic [THT]"]
  P4 = S1133 Si Photodiode [package="8mm Ceramic [THT]"]
  P5 = S1133 Si Photodiode [package="8mm Ceramic [THT]"]
  P6 = S1133 Si Photodiode [package="8mm Ceramic [THT]"]
  IC1 = SELECTOR_MULTIPLEXER [package=dil16]
  R13 = Resistor [tolerance=±5% resistance=1k package=THT]
  R14 = TRIMPOT [package=3386u]
  S2 = Toggle Switch [package=THT]
  R15 = Resistor [tolerance=±5% resistance=1k package=THT]

nets:
  N1: R1.Pin_0, Q1.D, IC1.A_1Y
  N2: R1.Pin_1, R2.Pin_1, R3.Pin_1, R4.Pin_1, R5.Pin_1, R6.Pin_1, P1.anode, P2.anode, P3.anode, P4.anode, P5.anode, P6.anode, IC1.A_2Y, IC1.P_GND, R14.CW
  N3: Q1.S, R7.Pin_1, P1.cathode
  N4: Q1.G, Q2.G, Q3.G, Q4.G, Q5.G, Q6.G, R7.Pin_0, R8.Pin_0, R9.Pin_0, R10.Pin_0, R11.Pin_0, R12.Pin_0, IC1.P_VCC
  N5: Q2.D, R2.Pin_0, IC1.A_1B
  N6: Q2.S, R8.Pin_1, P2.cathode
  N7: Q3.D, R4.Pin_0, IC1.A_1A
  N8: Q3.S, R9.Pin_1, P3.cathode
  N9: Q4.D, R3.Pin_0, IC1.A_!A!_B
  N10: Q4.S, R10.Pin_1, P6.cathode
  N11: Q5.D, R5.Pin_0, IC1.A_G
  N12: Q5.S, R11.Pin_1, P5.cathode
  N13: Q6.D, R6.Pin_0, IC1.A_4A
  N14: Q6.S, R12.Pin_1, P4.cathode
  N15: R13.Pin_0, R15.Pin_0
  N16: R13.Pin_1, R14.CCW
  N17: S2.L1, R15.Pin_1
  N18: S2.COM, S2.L2

notes:
  6 x photodiodes
  6 x laser diodes
  GND
  5V
  3V
  A1
  A2
  B1
  E7 E9 E11

custom parts:
  TRIMPOT: Various small potentiometers for set-and-forget applications
